# Fritzing sketch Prox Detect GPS (saved by Fritzing 0.9.10b)
breadboards: 1

parts:
  Part1 = SparkFun ESP8266 Thing
  Part2 = FTDI Basic Programmer
  JP1 = Header 3 [package=jst-3-pth]
  J1 = JST-03JQ-BT [part_number=JST-JQ-BT package=THT]  # not connected

nets:
  GND: Part1.GND, Part2.GND, JP1.2
  N1: Part1.VCC, JP1.1
  N2: Part1.RESET, Part2.DTR
  N3: Part1.U0TXO, Part2.RXI
  N4: Part1.U0RXI, Part2.TXO
  N5: Part1.USBVCC, Part2.POWER
  N6: Part1.GPIO13, JP1.3

notes:
  BLINK
  Not the exact part.
  GP1818MK is used.
  This is the footprint of the ESP8266 Thing DEV. The board used in the design is the ESP8266 Thing.
  Note: the VCC connection to the USB FTDI is 3V3.
  GPS Receiver
  Pin 1 - Red (VCC)
  Pin 2 - Black (GND)
  Pin 3 - White (TX)
